# Fritzing sketch software_implementation (saved by Fritzing 0.9.3b)
breadboards: 1

parts:
  LED1 = LED - 5mm [color="Red (633nm)" package="5 mm [THT]"]
  LED2 = LED - 5mm [color="Red (633nm)" package="5 mm [THT]"]
  R1 = Resistor [tolerance=±5% resistance=220 package=THT]
  R2 = Resistor [tolerance=±5% resistance=220 package=THT]
  SW1 = ENCODER_RGB_CA [package=encoder_led_3]  # not connected

nets:
  N1: LED1.cathode, R1.Pin_1
  N2: LED2.cathode, R2.Pin_1
  N3: R1.Pin_0, R2.Pin_0

notes:
  This is where the chip will go when I have the file
  These go to serial adapter RX and TX
  For rotary encoder: Blue is CLK and Green is DT
